// Logisim project Lab1_2.circ as structural Verilog: 1 circuit, main circuit main
module main (
  input  A,
  input  x,
  input  y,
  input  B,
  input  w,
  input  C,
  input  x_2,
  input  z,
  input  y_2,
  input  A_2,
  input  z_2,
  input  B_2,
  input  x_3,
  input  C_2,
  input  y_3,
  input  D,
  input  a_3,
  input  b_3,
  input  c_3,
  output Fa,
  output Fd,
  output Fb,
  output Fe,
  output Fc,
  output Ff
);

  wire and_1_out, and_2_out, and_3_out, and_4_out, and_5_out, and_7_out, and_8_out, and_9_out, and_10_out,
       and_11_out, and_12_out, and_14_out, and_15_out, not_1_out, not_2_out, not_3_out, or_1_out, or_2_out,
       or_5_out, or_6_out, or_7_out, or_8_out, or_9_out;

  not not_1 (not_1_out, C);
  not not_2 (not_2_out, y_3);
  and and_1 (and_1_out, A, B, C);
  and and_2 (and_2_out, A, B);
  and and_3 (and_3_out, A, B, not_1_out);
  and and_4 (and_4_out, x_2, y_2, z_2);
  and and_5 (and_5_out, x_2, z_2);
  or or_1 (or_1_out, x_3, not_2_out);
  or or_2 (or_2_out, x_3, y_3);
  and and_6 (Fc, or_1_out, or_2_out);
  or or_3 (Fa, and_1_out, and_2_out, and_3_out);
  or or_4 (Fb, and_4_out, and_5_out);
  not not_3 (not_3_out, z);
  and and_7 (and_7_out, w, z);
  and and_8 (and_8_out, w, not_3_out);
  and and_9 (and_9_out, A_2, B_2);
  and and_10 (and_10_out, C_2, D);
  and and_11 (and_11_out, B_2, C_2);
  and and_12 (and_12_out, A_2, D);
  or or_5 (or_5_out, a_3, c_3);
  or or_6 (or_6_out, a_3, b_3, c_3);
  or or_7 (or_7_out, and_7_out, and_8_out);
  or or_8 (or_8_out, and_9_out, and_10_out);
  or or_9 (or_9_out, and_11_out, and_12_out);
  and and_13 (Ff, or_5_out, or_6_out);
  and and_14 (and_14_out, x, y);
  and and_15 (and_15_out, x, or_7_out);
  and and_16 (Fe, or_8_out, or_9_out);
  or or_10 (Fd, and_14_out, and_15_out);

  // Notes on the sheet:
  //   ABC
  //   AB
  //   ABC'
  //   xyz
  //   xz
  //   x+y'
  //   x+y
  //   AB
  //   CD
  //   BC
  //   AD
  //   wz
  //   wz'
  //   a+c
  //   a+b+c
  //   AB+CD
  //   BC+AD
  //   xy
  //   x(wz+wz')
endmodule
