// Logisim project Lab2_1.circ as structural Verilog: 3 circuits, main circuit main
module main (
  input  A,
  input  B,
  input  A_2,
  input  B_2,
  input  Cin,
  output S,
  output Cout,
  output Cout_2,
  output S_2
);

  HALFADDER Half_Adder (.A(A), .B(B), .S(S), .Cout(Cout));
  FULLADDER Full_Adder (.A(A_2), .B(B_2), .Cin(Cin), .Cout(Cout_2), .S(S_2));
endmodule

module HALFADDER (
  input  A,
  input  B,
  output S,
  output Cout
);

  xor xor_1 (S, A, B);
  and and_1 (Cout, B, A);
endmodule

module FULLADDER (
  input  A,
  input  B,
  input  Cin,
  output Cout,
  output S
);

  wire and_1_out, and_2_out, and_3_out, and_4_out, and_5_out, and_6_out, and_7_out, and_8_out, not_1_out,
       not_2_out, not_3_out, not_4_out, not_5_out, not_6_out, not_7_out, not_8_out, not_9_out;

  not not_1 (not_1_out, A);
  not not_2 (not_2_out, B);
  not not_3 (not_3_out, Cin);
  not not_4 (not_4_out, A);
  not not_5 (not_5_out, B);
  not not_6 (not_6_out, A);
  not not_7 (not_7_out, Cin);
  not not_8 (not_8_out, B);
  not not_9 (not_9_out, Cin);
  and and_1 (and_1_out, not_1_out, B, Cin);
  and and_2 (and_2_out, A, not_2_out, Cin);
  and and_3 (and_3_out, A, B, not_3_out);
  and and_4 (and_4_out, A, B, Cin);
  and and_5 (and_5_out, not_4_out, not_5_out, Cin);
  and and_6 (and_6_out, not_6_out, B, not_7_out);
  and and_7 (and_7_out, A, not_8_out, not_9_out);
  and and_8 (and_8_out, A, B, Cin);
  or or_1 (Cout, and_1_out, and_2_out, and_3_out, and_4_out);
  or or_2 (S, and_5_out, and_6_out, and_7_out, and_8_out);
endmodule
