// Logisim project Lab2_2.circ as structural Verilog: 6 circuits, main circuit main
module main (
  input  [3:0] A_4,
  input  [3:0] B_4,
  input  Cin,
  input  [3:0] A_4_2,
  input  [3:0] B_4_2,
  input  Cin_2,
  output [3:0] S_4,
  output Cout,
  output [3:0] S_4_2,
  output Cout_2
);

  Hex_Digit_Display hex_digit_display_1 (.value(B_4));  // open: dp
  Hex_Digit_Display hex_digit_display_2 (.value(A_4_2));  // open: dp
  Hex_Digit_Display hex_digit_display_3 (.value(A_4));  // open: dp
  Hex_Digit_Display hex_digit_display_4 (.value(B_4_2));  // open: dp
  Hex_Digit_Display hex_digit_display_5 (.value(S_4));  // open: dp
  _4_bit_adder u_4_bit_adder_1 (.S_4(S_4), .A_4(A_4), .B_4(B_4), .Cin(Cin), .Cout(Cout));
  Hex_Digit_Display hex_digit_display_6 (.value(S_4_2));  // open: dp
  _4_bit_subtractor u_4_bit_subtractor_1 (.S_4(S_4_2), .A_4(A_4_2), .B_4(B_4_2), .Cin(Cin_2), .Cout(Cout_2));

  // Notes on the sheet:
  //   +
  //   -
  //   =
  //   =
endmodule

module _1_bit_adder (
  input  A,
  input  B,
  input  Cin,
  output Cout,
  output S
);

  wire nand_1_out, nand_2_out, nand_3_out, nand_4_out, nand_5_out, nand_6_out, nand_7_out, nand_8_out,
       nand_9_out, nand_11_out, nand_12_out, nand_13_out, nand_14_out;

  nand nand_1 (nand_1_out, B, Cin);
  nand nand_2 (nand_2_out, A, Cin);
  nand nand_3 (nand_3_out, A, B);
  nand nand_4 (nand_4_out, A, A);
  nand nand_5 (nand_5_out, B, B);
  nand nand_6 (nand_6_out, A, A);
  nand nand_7 (nand_7_out, Cin, Cin);
  nand nand_8 (nand_8_out, B, B);
  nand nand_9 (nand_9_out, Cin, Cin);
  nand nand_10 (Cout, nand_1_out, nand_2_out, nand_3_out);
  nand nand_11 (nand_11_out, nand_4_out, nand_5_out, Cin);
  nand nand_12 (nand_12_out, nand_6_out, B, nand_7_out);
  nand nand_13 (nand_13_out, A, nand_8_out, nand_9_out);
  nand nand_14 (nand_14_out, A, B, Cin);
  nand nand_15 (S, nand_11_out, nand_12_out, nand_13_out, nand_14_out);
endmodule

module FULLADDER (
  input  A,
  input  B,
  input  Cin,
  output Cout,
  output S
);

  wire and_1_out, and_2_out, and_3_out, and_4_out, and_5_out, and_6_out, and_7_out, not_1_out, not_2_out,
       not_3_out, not_4_out, not_5_out, not_6_out;

  and and_1 (and_1_out, B, Cin);
  and and_2 (and_2_out, A, Cin);
  and and_3 (and_3_out, A, B);
  not not_1 (not_1_out, A);
  not not_2 (not_2_out, B);
  not not_3 (not_3_out, A);
  not not_4 (not_4_out, Cin);
  not not_5 (not_5_out, B);
  not not_6 (not_6_out, Cin);
  or or_1 (Cout, and_1_out, and_2_out, and_3_out);
  and and_4 (and_4_out, not_1_out, not_2_out, Cin);
  and and_5 (and_5_out, not_3_out, B, not_4_out);
  and and_6 (and_6_out, A, not_5_out, not_6_out);
  and and_7 (and_7_out, A, B, Cin);
  or or_2 (S, and_4_out, and_5_out, and_6_out, and_7_out);
endmodule

module _4_bit_adder (
  input  [3:0] A_4,
  input  [3:0] B_4,
  input  Cin,
  output [3:0] S_4,
  output Cout
);

  wire fulladder_1_cout, fulladder_2_cout, fulladder_3_cout;

  Hex_Digit_Display hex_digit_display_1 (.value(A_4));  // open: dp
  Hex_Digit_Display hex_digit_display_2 (.value(B_4));  // open: dp
  Hex_Digit_Display hex_digit_display_3 (.value(S_4));  // open: dp
  FULLADDER fulladder_1 (.A(A_4[0]), .B(B_4[0]), .Cin(Cin), .Cout(fulladder_1_cout), .S(S_4[0]));
  FULLADDER fulladder_2 (.A(A_4[1]), .B(B_4[1]), .Cin(fulladder_1_cout), .Cout(fulladder_2_cout), .S(S_4[1]));
  FULLADDER fulladder_3 (.A(A_4[2]), .B(B_4[2]), .Cin(fulladder_2_cout), .Cout(fulladder_3_cout), .S(S_4[2]));
  FULLADDER fulladder_4 (.A(A_4[3]), .B(B_4[3]), .Cin(fulladder_3_cout), .Cout(Cout), .S(S_4[3]));

  // Notes on the sheet:
  //   +
  //   =
endmodule

module FULLSUBTRACTOR (
  input  A,
  input  B,
  input  Cin,
  output Cout,
  output S
);

  wire and_1_out, and_2_out, and_3_out, and_4_out, and_5_out, and_6_out, and_7_out, not_1_out, not_2_out,
       not_3_out, not_4_out, not_5_out, not_6_out, not_7_out, not_8_out;

  not not_1 (not_1_out, A);
  not not_2 (not_2_out, A);
  not not_3 (not_3_out, A);
  not not_4 (not_4_out, B);
  not not_5 (not_5_out, A);
  not not_6 (not_6_out, Cin);
  not not_7 (not_7_out, B);
  not not_8 (not_8_out, Cin);
  and and_1 (and_1_out, not_1_out, Cin);
  and and_2 (and_2_out, not_2_out, B);
  and and_3 (and_3_out, B, Cin);
  and and_4 (and_4_out, not_3_out, not_4_out, Cin);
  and and_5 (and_5_out, not_5_out, B, not_6_out);
  and and_6 (and_6_out, A, not_7_out, not_8_out);
  and and_7 (and_7_out, A, B, Cin);
  or or_1 (Cout, and_1_out, and_2_out, and_3_out);
  or or_2 (S, and_4_out, and_5_out, and_6_out, and_7_out);
endmodule

module _4_bit_subtractor (
  input  [3:0] A_4,
  input  [3:0] B_4,
  input  Cin,
  output [3:0] S_4,
  output Cout
);

  wire fullsubtractor_1_cout, fullsubtractor_2_cout, fullsubtractor_3_cout;

  Hex_Digit_Display hex_digit_display_1 (.value(A_4));  // open: dp
  Hex_Digit_Display hex_digit_display_2 (.value(B_4));  // open: dp
  Hex_Digit_Display hex_digit_display_3 (.value(S_4));  // open: dp
  FULLSUBTRACTOR fullsubtractor_1 (.A(A_4[0]), .B(B_4[0]), .Cin(Cin), .Cout(fullsubtractor_1_cout), .S(S_4[0]));
  FULLSUBTRACTOR fullsubtractor_2 (
    .A(A_4[1]), .B(B_4[1]), .Cin(fullsubtractor_1_cout), .Cout(fullsubtractor_2_cout), .S(S_4[1]));
  FULLSUBTRACTOR fullsubtractor_3 (
    .A(A_4[2]), .B(B_4[2]), .Cin(fullsubtractor_2_cout), .Cout(fullsubtractor_3_cout), .S(S_4[2]));
  FULLSUBTRACTOR fullsubtractor_4 (.A(A_4[3]), .B(B_4[3]), .Cin(fullsubtractor_3_cout), .Cout(Cout), .S(S_4[3]));

  // Notes on the sheet:
  //   -
  //   =
endmodule
