// Logisim project Week4.circ as structural Verilog: 1 circuit, main circuit main
module main (
);

  wire button_1_out, Clock_2_out, Clock_3_out, Clock_out;
  wire [2:0] counter_3_q, rom_2_data;
  wire [3:0] counter_1_q, rom_1_data;
  wire [5:0] counter_2_q;
  wire [6:0] rom_3_data;

  Counter #(.width(4), .max('hf)) counter_1 (
    .count(Clock_out), .Q(counter_1_q), .clk(Clock_out));  // open: load, D, carry, clr
  Clock Clock (.out(Clock_out));
  Clock Clock_2 (.out(Clock_2_out));
  Counter #(.width(6), .max('h3f)) counter_2 (
    .Q(counter_2_q), .clk(Clock_3_out), .clr(button_1_out));  // open: load, D, count, carry
  Clock Clock_3 (.out(Clock_3_out));
  Button button_1 (.out(button_1_out));
  Counter #(.width(3), .max('h7)) counter_3 (
    .count(Clock_2_out), .Q(counter_3_q), .clk(Clock_2_out));  // open: load, D, carry, clr
  ROM #(.addrWidth(4), .dataWidth(4)) rom_1 (.addr(counter_1_q), .data(rom_1_data));  // open: sel
  ROM #(.addrWidth(3), .dataWidth(3)) rom_2 (.addr(counter_3_q), .data(rom_2_data));  // open: sel
  ROM #(.addrWidth(6), .dataWidth(7)) rom_3 (.addr(counter_2_q), .data(rom_3_data));  // open: sel
  TTY tty_1 (.data(rom_3_data), .clk(Clock_3_out), .clr(button_1_out));  // open: we
  Hex_Digit_Display hex_digit_display_1 (.value(rom_1_data));  // open: dp
  LED led_1 (.in(rom_2_data[0]));
  LED led_2 (.in(rom_2_data[1]));
  LED led_3 (.in(rom_2_data[2]));

  // Notes on the sheet:
  //   Câu 1
  //   Câu 2
  //   Câu 3
  //   Counter
  //   Counter
  //   Counter
  //   Button
  //   ROM
  //   ROM
  //   ROM
  //   contents of rom_1 (hex, n*v repeats v):
  //   0 1 2 3 4 5 6 7 8 9 a b c d e f
  //   contents of rom_2 (hex, n*v repeats v):
  //   1 1 2 2 4 4 1 1
  //   contents of rom_3 (hex, n*v repeats v):
  //   58 69 6e 20 63 68 61 6f 20 63 61 63 20 62 61 6e 2e 20 a 43 68 75 63 20 63 61 63 20 62 61 6e 20 68 6f
  //   63 20 74 6f 74 21 a
  //   Splitter
  //   Hexa Digital Display
  //   Đèn đỏ
  //   Đèn vàng
  //   Đèn xanh
  //   TTY
endmodule
